# Fritzing sketch TinyLaserTurret (saved by Fritzing 0.8.3b)
circuit board: 5.20697cm x 5.15818cm
breadboards: 1

parts:
  U1 = Voltage Regulator - 5V [part_number=L78S05CV package="TO220 [THT]"]
  ATtiny85 = attiny85 [package=dip]
  C2 = Electrolytic Capacitor [capacitance=0.1mF package="100 mil [THT, electrolytic]"]
  Q1 = NPN-Transistor [part_number=BCU-81 package="TO92 [THT]"]
  R1 = Resistor [tolerance=±5% resistance=330 package=THT]
  JACK1 = 2.1mm Barrel Jack with Terminal Block
  Laser = LED - 5mm [color="Red (633nm)" part_number="5V laser module" package="5 mm [THT]"]
  J1 = female pin header, 4 pins [form="♀ (female)" part_number=WiiChuck]
  Pan = Basic Servo [part_number="Pan servo"]
  Tilt = Basic Servo [part_number="Tilt servo"]
  C1 = Electrolytic Capacitor [capacitance=0.1mF package="100 mil [THT, electrolytic]"]
  R2 = Resistor [tolerance=±5% resistance=4.7k package=THT]
  R3 = Resistor [tolerance=±5% resistance=4.7k package=THT]

nets:
  N1: U1.input_voltage, C2.+, JACK1.POS
  GND: U1.GND, ATtiny85.Pin_4, C2.-, Q1.E, JACK1.NEG, J1.pin1, Pan.gnd, Tilt.gnd, C1.-
  VCC: U1.output_voltage, ATtiny85.Pin_8, Laser.anode, J1.pin2, Pan.vcc, Tilt.vcc, C1.+, R2.Pin_0, R3.Pin_0
  N2: ATtiny85.Pin_2, Tilt.pulse
  N3: ATtiny85.Pin_3, Pan.pulse
  N4: ATtiny85.Pin_5, J1.pin3, R2.Pin_1
  N5: ATtiny85.Pin_6, R1.Pin_0
  N6: ATtiny85.Pin_7, J1.pin4, R3.Pin_1
  N7: Q1.B, R1.Pin_1
  N8: Q1.C, Laser.cathode

notes:
  Use a 5V red laser module, not a LED
  WiiChuck connector (I2C)
  - Black: GND
  - Orange: VCC
  - Green: Data (SDA)
  - Brown: Clock (SCL)
  Servo connectors
  - Orange: VCC
  - Black: GND
  - Yellow: Signal
